// Logisim project Projeto.circ as structural Verilog: 16 circuits, main circuit main
module somador_1bit (
  input  cin,
  input  A,
  input  B,
  output S,
  output cout
);

  wire and_1_out, and_2_out, xor_1_out;

  xor xor_1 (xor_1_out, A, B);
  and and_1 (and_1_out, A, B);
  xor xor_2 (S, cin, xor_1_out);
  and and_2 (and_2_out, cin, xor_1_out);
  or or_1 (cout, and_2_out, and_1_out);
endmodule

module main (
);

  wire clock_1_out, not_1_out, not_2_out, O_q, Reset_out, uc_1_ac, \uc_1_direção , uc_1_ir, uc_1_load,
       \uc_1_modo_de_endereçamento , uc_1_pc, uc_1_r_w, uc_1_ram, uc_1_rst_pc, ula_1_overflow, ula_1_zero,
       Z_q;
  wire [2:0] uc_1_opcode;
  wire [3:0] ac_1_s, mux_1_s, PC_q, ram_1_data, uc_1_dados, uc_1_operando, ula_1_s;
  wire [7:0] ir_1_s, rom_1_data;

  not not_1 (not_1_out, uc_1_load);
  Clock clock_1 (.out(clock_1_out));
  Button Reset (.out(Reset_out));
  Counter #(.width(4), .max('hf), .trigger("falling")) PC (
    .load(uc_1_load), .D(uc_1_dados), .count(not_1_out), .Q(PC_q), .clk(uc_1_pc), .clr(uc_1_rst_pc));  // open: carry
  UC uc_1 (
    .Clock(clock_1_out), .Reset(Reset_out), .Rst_PC(uc_1_rst_pc), .Dados(uc_1_dados),
    .Operando(uc_1_operando), .\Direção (\uc_1_direção ), .Opcode(uc_1_opcode), .\Instrução (ir_1_s),
    .IR(uc_1_ir), .PC(uc_1_pc), .AC(uc_1_ac), .RAM(uc_1_ram), .Load(uc_1_load), .O(O_q), .Z(Z_q),
    .R_W(uc_1_r_w), .\Modo_de_Endereçamento (\uc_1_modo_de_endereçamento ));
  ROM #(.addrWidth(4)) rom_1 (.addr(PC_q), .data(rom_1_data));  // open: sel
  // Probe on ac_1_s
  IR ir_1 (.S(ir_1_s), .Clock(uc_1_ir), .E(rom_1_data));
  ULA ula_1 (
    .D(\uc_1_direção ), .B(mux_1_s), .A(ac_1_s), .in_4(uc_1_opcode), .S(ula_1_s), .Zero(ula_1_zero),
    .Overflow(ula_1_overflow));
  // Probe on ula_1_s
  AC ac_1 (.Clock(uc_1_ac), .E(ula_1_s), .S(ac_1_s));
  // Probe on mux_1_s
  // Probe on ram_1_data
  MUX mux_1 (.E(uc_1_operando), .C(\uc_1_modo_de_endereçamento ), .D(ram_1_data), .S(mux_1_s));
  D_Flip_Flop O (.clk(uc_1_ac), .D(ula_1_overflow), .Q(O_q));  // open: Qn, preset, en, reset
  D_Flip_Flop Z (.clk(uc_1_ac), .D(ula_1_zero), .Q(Z_q));  // open: Qn, preset, en, reset
  RAM #(.addrWidth(4), .dataWidth(4)) ram_1 (
    .addr(uc_1_operando), .data(ram_1_data), .clk(uc_1_ram), .ld(uc_1_r_w));  // open: sel, clr
  not not_2 (not_2_out, uc_1_r_w);
  Buff buff_1 (.E(ac_1_s), .in_2(not_2_out), .S(ram_1_data));

  // Notes on the sheet:
  //   contents of rom_1 (hex, n*v repeats v):
  //   8 b1 b1 b1 e0
  //   0
  //   1
  //   2
  //   3
  //   4
  //   5
  //   6
  //   7
  //   8
  //   9
  //   A
  //   B
  //   C
  //   D
  //   E
  //   F
  //   Instruction Set
  //   0
  //   MOV
  //   000
  //   1
  //   000
  //   MOV
  //   0
  //   ADD
  //   001
  //   1
  //   001
  //   ADD
  //   010
  //   0
  //   SUB
  //   1
  //   010
  //   SUB
  //   0
  //   OR
  //   011
  //   1
  //   OR
  //   011
  //   0
  //   100
  //   NOT
  //   100
  //   NOT
  //   1
  //   0
  //   101
  //   SHF
  //   1
  //   SHF
  //   101
  //   0
  //   110
  //   JPZ
  //   JPO
  //   110
  //   1
  //   111
  //   GO
  //   0
  //   STR
  //   1
  //   111
  //   AC <= X
  //   AC <= M(X)
  //   AC <= AC+X
  //   AC <= AC+M(X)
  //   AC <= AC-X
  //   AC <= AC-M(X)
  //   AC <= AC OR X
  //   AC <= AC OR M(X)
  //   AC <= NOT X
  //   AC <= NOT M( X)
  //   AC <= AC << Q
  //   AC <= AC >> Q
  //   PC <= X SE FLAG Z
  //   PC <= X SE FLAG O
  //   PC <= X
  //   M(X) <= AC 
endmodule

module somador_4bit (
  input  [3:0] B,
  input  [3:0] A,
  output Overflow,
  output [3:0] S
);

  wire somador_1bit_2_cout, somador_1bit_3_cout, somador_1bit_4_cout;

  somador_1bit somador_1bit_1 (.cin(somador_1bit_2_cout), .A(A[3]), .B(B[3]), .S(S[3]), .cout(Overflow));
  somador_1bit somador_1bit_2 (.cin(somador_1bit_3_cout), .A(A[2]), .B(B[2]), .S(S[2]), .cout(somador_1bit_2_cout));
  somador_1bit somador_1bit_3 (.cin(somador_1bit_4_cout), .A(A[1]), .B(B[1]), .S(S[1]), .cout(somador_1bit_3_cout));
  somador_1bit somador_1bit_4 (.cin(1'b0), .A(A[0]), .B(B[0]), .S(S[0]), .cout(somador_1bit_4_cout));
endmodule

module subtrator_1bit (
  input  A,
  input  B,
  input  C,
  output S,
  output Vai_1
);

  wire and_1_out, and_2_out, or_1_out, xor_1_out;

  xor xor_1 (xor_1_out, C, B);
  or or_1 (or_1_out, C, B);
  xor xor_2 (S, xor_1_out, A);
  and and_1 (and_1_out, or_1_out, ~A);  // AND_Gate
  and and_2 (and_2_out, C, B);
  or or_2 (Vai_1, and_1_out, and_2_out);
endmodule

module subtrator_4bit (
  input  [3:0] B,
  input  [3:0] A,
  output Overflow,
  output [3:0] S
);

  wire subtrator_1bit_2_vai_1, subtrator_1bit_3_vai_1, subtrator_1bit_4_vai_1;

  subtrator_1bit subtrator_1bit_1 (.S(S[3]), .Vai_1(Overflow), .A(A[3]), .B(B[3]), .C(subtrator_1bit_2_vai_1));
  subtrator_1bit subtrator_1bit_2 (
    .S(S[2]), .Vai_1(subtrator_1bit_2_vai_1), .A(A[2]), .B(B[2]), .C(subtrator_1bit_3_vai_1));
  subtrator_1bit subtrator_1bit_3 (
    .S(S[1]), .Vai_1(subtrator_1bit_3_vai_1), .A(A[1]), .B(B[1]), .C(subtrator_1bit_4_vai_1));
  subtrator_1bit subtrator_1bit_4 (.S(S[0]), .Vai_1(subtrator_1bit_4_vai_1), .A(A[0]), .B(B[0]), .C(1'b0));
endmodule

module Rot_Esq (
  input  [3:0] abcd,
  input  [1:0] xy,
  output [3:0] ABCD_2
);

  wire and_1_out, and_2_out, and_3_out, and_4_out, and_5_out, and_6_out, and_7_out, and_8_out, and_9_out;

  and and_1 (and_1_out, ~xy[1], ~xy[0], abcd[3]);  // AND_Gate
  and and_2 (and_2_out, ~xy[1], xy[0], abcd[2]);  // AND_Gate
  and and_3 (and_3_out, xy[1], ~xy[0], abcd[1]);  // AND_Gate
  and and_4 (and_4_out, xy[1], xy[0], abcd[0]);
  and and_5 (and_5_out, ~xy[1], ~xy[0], abcd[2]);  // AND_Gate
  and and_6 (and_6_out, ~xy[1], xy[0], abcd[1]);  // AND_Gate
  and and_7 (and_7_out, xy[1], ~xy[0], abcd[0]);  // AND_Gate
  and and_8 (and_8_out, ~xy[1], ~xy[0], abcd[1]);  // AND_Gate
  and and_9 (and_9_out, ~xy[1], xy[0], abcd[0]);  // AND_Gate
  and and_10 (ABCD_2[0], ~xy[1], ~xy[0], abcd[0]);  // AND_Gate
  or or_1 (ABCD_2[3], and_1_out, and_2_out, and_3_out, and_4_out);
  or or_2 (ABCD_2[2], and_5_out, and_6_out, and_7_out);
  or or_3 (ABCD_2[1], and_8_out, and_9_out);
endmodule

module Rot_Dir (
  input  [3:0] abcd,
  input  [1:0] xy,
  output [3:0] ABCD_2
);

  wire and_1_out, and_2_out, and_3_out, and_4_out, and_5_out, and_6_out, and_7_out, and_8_out, and_9_out;

  and and_1 (and_1_out, ~xy[1], ~xy[0], abcd[0]);  // AND_Gate
  and and_2 (and_2_out, ~xy[1], xy[0], abcd[1]);  // AND_Gate
  and and_3 (and_3_out, xy[1], ~xy[0], abcd[2]);  // AND_Gate
  and and_4 (and_4_out, xy[1], xy[0], abcd[3]);
  and and_5 (and_5_out, ~xy[1], ~xy[0], abcd[1]);  // AND_Gate
  and and_6 (and_6_out, ~xy[1], xy[0], abcd[2]);  // AND_Gate
  and and_7 (and_7_out, xy[1], ~xy[0], abcd[3]);  // AND_Gate
  and and_8 (and_8_out, ~xy[1], ~xy[0], abcd[2]);  // AND_Gate
  and and_9 (and_9_out, ~xy[1], xy[0], abcd[3]);  // AND_Gate
  and and_10 (ABCD_2[3], ~xy[1], ~xy[0], abcd[3]);  // AND_Gate
  or or_1 (ABCD_2[0], and_1_out, and_2_out, and_3_out, and_4_out);
  or or_2 (ABCD_2[1], and_5_out, and_6_out, and_7_out);
  or or_3 (ABCD_2[2], and_8_out, and_9_out);
endmodule

module Dec_3x8 (
  input  [2:0] ABC,
  output S0,
  output S1,
  output S2,
  output S3,
  output S4,
  output S5,
  output S6,
  output S7
);

  wire not_1_out, not_2_out, not_3_out, not_4_out, not_5_out, not_6_out, not_7_out, not_8_out, not_9_out,
       not_10_out, not_11_out, not_12_out;

  not not_1 (not_1_out, ABC[2]);
  not not_2 (not_2_out, ABC[1]);
  not not_3 (not_3_out, ABC[0]);
  not not_4 (not_4_out, ABC[2]);
  not not_5 (not_5_out, ABC[1]);
  not not_6 (not_6_out, ABC[2]);
  not not_7 (not_7_out, ABC[0]);
  not not_8 (not_8_out, ABC[2]);
  not not_9 (not_9_out, ABC[1]);
  not not_10 (not_10_out, ABC[0]);
  not not_11 (not_11_out, ABC[1]);
  not not_12 (not_12_out, ABC[0]);
  and and_1 (S7, ABC[2], ABC[1], ABC[0]);
  and and_2 (S0, not_1_out, not_2_out, not_3_out);
  and and_3 (S1, not_4_out, not_5_out, ABC[0]);
  and and_4 (S2, not_6_out, ABC[1], not_7_out);
  and and_5 (S3, not_8_out, ABC[1], ABC[0]);
  and and_6 (S4, ABC[2], not_9_out, not_10_out);
  and and_7 (S5, ABC[2], not_11_out, ABC[0]);
  and and_8 (S6, ABC[2], ABC[1], not_12_out);
endmodule

module Buff (
  input  [3:0] E,
  input  in_2,
  output [3:0] S
);

  assign S[3] = in_2 ? E[3] : 1'bz;  // Controlled_Buffer controlled_buffer_1
  assign S[2] = in_2 ? E[2] : 1'bz;  // Controlled_Buffer controlled_buffer_2
  assign S[1] = in_2 ? E[1] : 1'bz;  // Controlled_Buffer controlled_buffer_3
  assign S[0] = in_2 ? E[0] : 1'bz;  // Controlled_Buffer controlled_buffer_4
endmodule

module Or_4bit (
  input  [3:0] B,
  input  [3:0] A,
  output [3:0] S
);

  or or_1 (S[3], B[3], A[3]);
  or or_2 (S[2], B[2], A[2]);
  or or_3 (S[1], B[1], A[1]);
  or or_4 (S[0], B[0], A[0]);
endmodule

module Not (
  input  [3:0] E,
  output [3:0] S
);

  not not_1 (S[2], E[2]);
  not not_2 (S[3], E[3]);
  not not_3 (S[0], E[0]);
  not not_4 (S[1], E[1]);
endmodule

module ULA (
  input  D,
  input  [3:0] B,
  input  [3:0] A,
  input  [2:0] in_4,
  output Overflow,
  output [3:0] S,
  output Zero
);

  wire and_1_out, and_2_out, dec_3x8_1_s0, dec_3x8_1_s1, dec_3x8_1_s2, dec_3x8_1_s3, dec_3x8_1_s4,
       dec_3x8_1_s5, dec_3x8_1_s6, dec_3x8_1_s7, not_2_out, somador_4bit_1_overflow,
       subtrator_4bit_1_overflow;
  wire [3:0] buff_7_s, not_1_s, or_4bit_1_s, rot_dir_1_abcd_2, rot_esq_1_abcd_2, somador_4bit_1_s,
       subtrator_4bit_1_s;

  or or_1 (Overflow, and_1_out, and_2_out);
  and and_1 (and_1_out, somador_4bit_1_overflow, dec_3x8_1_s1);
  and and_2 (and_2_out, subtrator_4bit_1_overflow, dec_3x8_1_s2);
  Dec_3x8 dec_3x8_1 (
    .ABC(in_4), .S0(dec_3x8_1_s0), .S1(dec_3x8_1_s1), .S2(dec_3x8_1_s2), .S3(dec_3x8_1_s3),
    .S4(dec_3x8_1_s4), .S5(dec_3x8_1_s5), .S6(dec_3x8_1_s6), .S7(dec_3x8_1_s7));
  Buff buff_1 (.E(B), .in_2(dec_3x8_1_s0), .S(S));
  somador_4bit somador_4bit_1 (.A(A), .Overflow(somador_4bit_1_overflow), .B(B), .S(somador_4bit_1_s));
  Buff buff_2 (.E(somador_4bit_1_s), .in_2(dec_3x8_1_s1), .S(S));
  nor nor_1 (Zero, S[0], S[1], S[2], S[3], dec_3x8_1_s6, dec_3x8_1_s7);
  subtrator_4bit subtrator_4bit_1 (.A(A), .Overflow(subtrator_4bit_1_overflow), .B(B), .S(subtrator_4bit_1_s));
  Or_4bit or_4bit_1 (.A(A), .B(B), .S(or_4bit_1_s));
  Buff buff_3 (.E(or_4bit_1_s), .in_2(dec_3x8_1_s3), .S(S));
  Buff buff_4 (.E(subtrator_4bit_1_s), .in_2(dec_3x8_1_s2), .S(S));
  Not not_1 (.E(B), .S(not_1_s));
  Buff buff_5 (.E(not_1_s), .in_2(dec_3x8_1_s4), .S(S));
  not not_2 (not_2_out, D);
  Rot_Esq rot_esq_1 (.abcd(A), .xy(B[1:0]), .ABCD_2(rot_esq_1_abcd_2));
  Rot_Dir rot_dir_1 (.abcd(A), .xy(B[1:0]), .ABCD_2(rot_dir_1_abcd_2));
  Buff buff_6 (.E(buff_7_s), .in_2(dec_3x8_1_s5), .S(S));
  Buff buff_7 (.E(rot_esq_1_abcd_2), .in_2(not_2_out), .S(buff_7_s));
  Buff buff_8 (.E(rot_dir_1_abcd_2), .in_2(D), .S(buff_7_s));
endmodule

module AC (
  input  Clock,
  input  [3:0] E,
  output [3:0] S
);

  D_Flip_Flop D3 (.clk(Clock), .D(E[3]), .Q(S[3]));  // open: Qn, preset, en, reset
  D_Flip_Flop D2 (.clk(Clock), .D(E[2]), .Q(S[2]));  // open: Qn, preset, en, reset
  D_Flip_Flop D1 (.clk(Clock), .D(E[1]), .Q(S[1]));  // open: Qn, preset, en, reset
  D_Flip_Flop D0 (.clk(Clock), .D(E[0]), .Q(S[0]));  // open: Qn, preset, en, reset
endmodule

module MUX (
  input  [3:0] E,
  input  [3:0] D,
  input  C,
  output [3:0] S
);

  wire not_1_out;

  Buff buff_1 (.E(E), .in_2(not_1_out), .S(S));
  not not_1 (not_1_out, C);
  Buff buff_2 (.E(D), .in_2(C), .S(S));
endmodule

module IR (
  input  Clock,
  input  [7:0] E,
  output [7:0] S
);

  D_Flip_Flop #(.trigger("falling")) D7 (.clk(Clock), .D(E[7]), .Q(S[7]));  // open: Qn, preset, en, reset
  D_Flip_Flop #(.trigger("falling")) D6 (.clk(Clock), .D(E[6]), .Q(S[6]));  // open: Qn, preset, en, reset
  D_Flip_Flop #(.trigger("falling")) D5 (.clk(Clock), .D(E[5]), .Q(S[5]));  // open: Qn, preset, en, reset
  D_Flip_Flop #(.trigger("falling")) D4 (.clk(Clock), .D(E[4]), .Q(S[4]));  // open: Qn, preset, en, reset
  D_Flip_Flop #(.trigger("falling")) D3 (.clk(Clock), .D(E[3]), .Q(S[3]));  // open: Qn, preset, en, reset
  D_Flip_Flop #(.trigger("falling")) D2 (.clk(Clock), .D(E[2]), .Q(S[2]));  // open: Qn, preset, en, reset
  D_Flip_Flop #(.trigger("falling")) D1 (.clk(Clock), .D(E[1]), .Q(S[1]));  // open: Qn, preset, en, reset
  D_Flip_Flop #(.trigger("falling")) D0 (.clk(Clock), .D(E[0]), .Q(S[0]));  // open: Qn, preset, en, reset
endmodule

module UC (
  input  [7:0] \Instrução ,
  input  Z,
  input  Clock,
  input  Reset,
  input  O,
  output [3:0] Dados,
  output [3:0] Operando,
  output \Direção ,
  output IR,
  output PC,
  output AC,
  output RAM,
  output \Modo_de_Endereçamento ,
  output Rst_PC,
  output [2:0] Opcode,
  output Load,
  output R_W
);

  wire GOTO_out, JPO_out, JPZ_out, nand_1_out;
  wire [1:0] counter_1_q;

  Counter #(.width(2), .max('h3)) counter_1 (.Q(counter_1_q), .clk(Clock), .clr(Reset));  // open: load, D, count, carry
  and and_1 (PC, ~counter_1_q[1], counter_1_q[0]);  // AND_Gate
  and and_2 (IR, ~counter_1_q[1], ~counter_1_q[0]);  // AND_Gate
  nand STOR (R_W, AC, \Instrução [7], \Instrução [6], \Instrução [4], \Instrução [5]);
  and and_3 (AC, counter_1_q[1], ~counter_1_q[0]);  // AND_Gate
  and JPO (JPO_out, \Instrução [7], \Instrução [6], ~\Instrução [5], \Instrução [4], PC, O);  // AND_Gate
  and and_4 (RAM, counter_1_q[1], counter_1_q[0]);
  and JPZ (JPZ_out, \Instrução [7], \Instrução [6], ~\Instrução [5], ~\Instrução [4], PC, Z);  // AND_Gate
  and GOTO (GOTO_out, \Instrução [7], \Instrução [6], \Instrução [5], ~\Instrução [4], PC);  // AND_Gate
  or or_1 (Load, GOTO_out, JPZ_out, JPO_out);
  nand nand_1 (nand_1_out, \Instrução [4], \Instrução [5], ~\Instrução [6], \Instrução [7]);  // NAND_Gate
  and and_5 (\Modo_de_Endereçamento , \Instrução [4], nand_1_out);

  assign Dados = \Instrução [3:0];
  assign \Direção  = \Instrução [4];
  assign Opcode = \Instrução [7:5];
  assign Operando = \Instrução [3:0];
  assign Rst_PC = Reset;
endmodule
